# Fritzing sketch fire_sensing_circuit (saved by Fritzing 0.9.3b)
breadboards: 1

parts:
  Raspberry_Pi_1 = Raspberry Pi 3 [part_number=RPI-3-V1.2]
  Part1 = KY-015 Temperature & Humidity Sensor Module [package="Breakout board"]
  Mod1 = KY-026 Flame Sensor Module [package="Breakout board"]
  부품1 = Passive Buzzer

nets:
  N1: Raspberry_Pi_1.GIPO17, Mod1.D0
  N2: Raspberry_Pi_1.GIPO27, Part1.S
  N3: Raspberry_Pi_1.GIPO22, 부품1.S
  GND: Raspberry_Pi_1.GND, Part1.-, Mod1.G, 부품1.GND
  5V: Raspberry_Pi_1.5V, Part1.Vin, Mod1.+, 부품1.NC

custom parts:
  KY-015 Temperature & Humidity Sensor Module: KY-015 temperature and humidity sensor module, provides a low-latency serial interface to measure humidity and temperature.
  KY-026 Flame Sensor Module: KY-026 Flame Sensor Module reacts in the presence of fire.
